# Fritzing sketch Two-Way-Communicator (saved by Fritzing 0.9.0b)
breadboards: 1

parts:
  Part1 = Intel Galileo
  Part2 = Breakout Board for Electret Microphone
  U1 = TRANSISTOR_NPN_2 [package=to-92]
  LED1 = LED - 3mm [color="Red (633nm)" package="3 mm [THT]"]
  R1 = Resistor [tolerance=±5% resistance=220 package="0603 [SMD]"]
  U2 = SLIDER [package=slider]
  Part3 = Mono Audio Amp Breakout
  MCP1 = MCP4921 [package="DIP (Dual Inline) [THT]"]
  LED2 = LED - 3mm [color="Red (633nm)" package="3 mm [THT]"]
  R2 = Resistor [tolerance=±5% resistance=220 package="0603 [SMD]"]
  S1 = Round Pushbutton
  SP1 = SPEAKER [package=pcb_mount_speaker]

nets:
  N1: Part1.A0, Part2.AUD
  N2: Part1.D11_PWM/MOSI, MCP1.SDAT
  N3: Part1.D13/SCK, MCP1.SCLK
  N4: Part1.D2, MCP1./CS
  N5: Part1.D3_PWM, S1.leg0
  N6: Part1.D4, LED2.anode
  VCC: Part1.5V, Part2.VCC, U1.E, MCP1.Vcc, MCP1.Vref, S1.leg1
  GND: Part1.GND, Part2.GND, R1.Pin_1, Part3.IN-, MCP1./LDAC, MCP1.AVss, R2.Pin_1
  N7: U1.C, LED1.anode
  N8: U1.B, Part3.IN+, MCP1.Vout
  N9: LED1.cathode, R1.Pin_0
  N10: U2.E, Part3.VOL+
  N11: U2.S, Part3.VOL
  N12: U2.A, Part3.VOL-
  N13: Part3.OUT+, SP1.-
  N14: Part3.OUT-, SP1.+
  N15: LED2.cathode, R2.Pin_0

notes:
  Rev 2, Running
  Windows 8.1
  With Lightning Improvements

custom parts:
  Mono Audio Amp Breakout: Description: This tiny audio amplifier is based on the Texas Instruments TPA2005D1. Its efficient class-D operation means low heat and long battery life. It can drive an 8-Ohm speaker at up to 1.4 Watts; it won't shake a stadium, but it will provide plenty of volume for your audio projects. The fully-differential inputs are safe for floating audio signals such as from our MP3 Shield, and can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
  MCP4921: MCP4921, 12 bit SPI-capabale DAC
